// Logisim project processor.circ as structural Verilog: 8 circuits, main circuit main
module main (
  input  [31:0] Instruction,
  input  [31:0] LOAD_DATA1,
  output [31:0] out_3
);

  wire and_1_out, bypasslogic_1_out_3, bypasslogic_2_out_3, bypasslogic_3_out_3, clk, comparator_1_eq,
       comparator_2_eq, comparator_3_eq, not_1_out, not_2_out, RS1En, RS1En_EX, RS2En, RS2En_EX, stall, WrEn,
       WrEn_EX, WrEn_MEM, WrEn_WB;
  wire [2:0] FUNCT3, FUNCT3_EX, register_14_q;
  wire [3:0] FunctSel;
  wire [4:0] RD, RD_EX, RD_MEM, RS1, RS1_EX, RS2, RS2_EX;
  wire [6:0] FUNCT7, OPCODE, opcode_EX;
  wire [31:0] immediate, RAM_DATA, RAM_DATA_EX, register_1_q, register_2_q, register_file_1_rs1_2,
       register_file_1_rs2_2, RS1_Input, RS1EX, RS2_Input, RS2EX, stallCLK, WB_Data, WB_MEM;

  Clock clock_1 (.out(clk));
  Register #(.width(32)) register_1 (.D(Instruction), .Q(register_1_q), .clk(clk));  // open: en, clr
  Control control_1 (
    .Instruction(register_1_q), .A_Sel(RS1En), .B_Sel(RS2En), .WrEn(WrEn));  // open: BRLT, BREQ, MemRW, RWEn, PC_Sel
  Register #(.width(32)) register_2 (.D(LOAD_DATA1), .Q(register_2_q), .clk(clk));  // open: en, clr
  Comparator #(.width(7)) comparator_1 (.a(OPCODE), .b(7'b0000011), .eq(comparator_1_eq));  // open: gt, lt
  Register_File register_file_1 (
    .Write_Data(WB_Data), .RS1(RS1), .RS2(RS2), .RD(RD), .WrEn(WrEn_EX), .clk(clk),
    .RS1_2(register_file_1_rs1_2), .RS2_2(register_file_1_rs2_2));  // open: RD_2
  Decode decode_1 (
    .Instruction(register_1_q), .OPCODE(OPCODE), .RD(RD), .FUNCT3(FUNCT3), .RS1(RS1), .RS2(RS2),
    .FUNCT7(FUNCT7), .immediate(immediate));
  Multiplexer #(.width(32)) multiplexer_1 (
    .in0(register_2_q), .in1(immediate), .out(RAM_DATA), .sel(comparator_1_eq));  // open: en
  Multiplexer #(.width(32)) multiplexer_2 (.in0(32'h1), .in1({32{1'b0}}), .out(stallCLK), .sel(and_1_out));  // open: en
  and and_1 (and_1_out, WrEn, stall);
  Comparator #(.width(5)) comparator_2 (.a(RS1), .b(RD_EX), .eq(comparator_2_eq));  // open: gt, lt
  Comparator #(.width(5)) comparator_3 (.a(RD_EX), .b(RS2), .eq(comparator_3_eq));  // open: gt, lt
  Multiplexer #(.width(32)) multiplexer_3 (
    .in0(register_file_1_rs1_2), .in1({32{1'b0}}), .out(RS1_Input), .sel(not_1_out));  // open: en
  not not_1 (not_1_out, RS1En);
  Multiplexer #(.width(32)) multiplexer_4 (
    .in0(register_file_1_rs2_2), .in1({32{1'b0}}), .out(RS2_Input), .sel(not_2_out));  // open: en
  not not_2 (not_2_out, RS2En);
  or or_1 (stall, comparator_2_eq, comparator_3_eq);
  Multiplexer #(.width(5)) multiplexer_5 (.sel(bypasslogic_1_out_3));  // open: in0, in1, out, en
  bypassLogic bypasslogic_1 (.rs12_D(RS1), .rd_EX(RD_EX), .out_3(bypasslogic_1_out_3));
  bypassLogic bypasslogic_2 (.rs12_D(RS1), .rd_EX(RD_EX), .out_3(bypasslogic_2_out_3));
  bypassLogic bypasslogic_3 (.rs12_D(RS2), .rd_EX(RD_EX), .out_3(bypasslogic_3_out_3));
  Register #(.width(1)) register_3 (.D(RS1En), .Q(RS1En_EX), .clk(clk));  // open: en, clr
  Register #(.width(1)) register_4 (.D(RS2En), .Q(RS2En_EX), .clk(clk));  // open: en, clr
  Register #(.width(1)) register_5 (.D(WrEn), .Q(WrEn_EX), .clk(clk));  // open: en, clr
  Multiplexer #(.width(32)) multiplexer_6 (
    .in0(RS1_Input), .in1(WB_Data), .out(RS1_Input), .sel(bypasslogic_2_out_3));  // open: en
  Multiplexer #(.width(32)) multiplexer_7 (
    .in0(RS2_Input), .in1(WB_Data), .out(RS2_Input), .sel(bypasslogic_3_out_3));  // open: en
  Register #(.width(1)) register_6 (.D(WrEn_EX), .Q(WrEn_MEM), .clk(clk));  // open: en, clr
  Register #(.width(32)) register_7 (.D(RS1_Input), .Q(RS1EX), .clk(clk));  // open: en, clr
  Register #(.width(32)) register_8 (.D(RS2_Input), .Q(RS2EX), .clk(clk));  // open: en, clr
  Register #(.width(7)) register_9 (.D(OPCODE), .Q(opcode_EX), .clk(clk));  // open: en, clr
  Register #(.width(5)) register_10 (.D(RD), .Q(RD_EX), .clk(clk));  // open: en, clr
  Register #(.width(3)) register_11 (.D(FUNCT3), .Q(FUNCT3_EX), .clk(clk));  // open: en, clr
  Register #(.width(5)) register_12 (.D(RS1), .Q(RS1_EX), .clk(clk));  // open: en, clr
  Register #(.width(5)) register_13 (.D(RS2), .Q(RS2_EX), .clk(clk));  // open: en, clr
  Register #(.width(7)) register_14 (.D(FUNCT7), .Q({FunctSel, register_14_q}), .clk(clk));  // open: en, clr
  Register #(.width(32)) register_15 (.D(RAM_DATA), .Q(RAM_DATA_EX), .clk(clk));  // open: en, clr
  Register #(.width(1)) register_16 (.D(WrEn_MEM), .Q(WrEn_WB), .clk(clk));  // open: en, clr
  ALU alu_1 (
    .RS1(RS1EX), .ASel(RS1En_EX), .RS2(RS2EX), .BSel(RS2En_EX), .RAM_DATA(RAM_DATA_EX), .SELECTOR(FunctSel),
    .out_7(WB_Data));
  Register #(.width(5)) register_17 (.D(RD_EX), .Q(RD_MEM), .clk(clk));  // open: en, clr
  Register #(.width(32)) register_18 (.D(WB_Data), .Q(WB_MEM), .clk(clk));  // open: en, clr
  MEM mem_1 (.Address(RD_MEM), .Write_Data(WB_MEM), .WriteEn(WrEn_MEM), .clk(clk), .Read_Data(out_3));
endmodule

// Arithmetic Logic Unit
module ALU (
  input  [31:0] RS1,
  input  ASel,
  input  [31:0] RS2,
  input  BSel,
  input  [31:0] RAM_DATA,
  input  [3:0] SELECTOR,
  output [31:0] out_7
);

  wire comparator_1_eq, comparator_1_gt, comparator_1_lt;
  wire [31:0] adder_1_out, and_1_out, bit_extender_1_out, bit_extender_2_out, bit_extender_3_out,
       divider_1_out, multiplexer_1_out, multiplexer_2_out, multiplier_1_out, or_1_out, shifter_1_out,
       shifter_2_out, shifter_3_out, subtractor_1_out, undriven, xor_1_out;

  Multiplexer #(.width(32)) multiplexer_1 (
    .in0({32{1'b0}}), .in1(RS1), .out(multiplexer_1_out), .sel(ASel));  // open: en
  Multiplexer #(.width(32)) multiplexer_2 (.in0(RAM_DATA), .in1(RS2), .out(multiplexer_2_out), .sel(BSel));  // open: en
  Adder #(.width(32)) adder_1 (.a(multiplexer_1_out), .b(multiplexer_2_out), .out(adder_1_out));  // open: cin, cout
  Subtractor #(.width(32)) subtractor_1 (
    .a(undriven), .b(multiplexer_2_out), .out(subtractor_1_out));  // open: bin, bout
  Multiplier #(.width(32)) multiplier_1 (
    .a(undriven), .b(multiplexer_2_out), .out(multiplier_1_out));  // open: cin, cout
  Divider #(.width(32)) divider_1 (.a(undriven), .b(multiplexer_2_out), .out(divider_1_out));  // open: upper, rem
  assign and_1_out = multiplexer_1_out & RS2;  // AND_Gate and_1, 32 bits wide
  assign xor_1_out = multiplexer_1_out ^ RS2;  // XOR_Gate xor_1, 32 bits wide
  assign or_1_out = multiplexer_1_out | RS2;  // OR_Gate or_1, 32 bits wide
  Comparator #(.width(32)) comparator_1 (
    .a(multiplexer_1_out), .b(RS2), .gt(comparator_1_gt), .eq(comparator_1_eq), .lt(comparator_1_lt));
  Shifter #(.width(32)) shifter_1 (.in(multiplexer_1_out), .\dist (RS2[4:0]), .out(shifter_1_out));
  Shifter #(.width(32)) shifter_2 (.in(multiplexer_1_out), .\dist (RS2[4:0]), .out(shifter_2_out));
  Shifter #(.width(32), .shift("ar")) shifter_3 (.in(multiplexer_1_out), .\dist (RS2[4:0]), .out(shifter_3_out));
  assign bit_extender_1_out = {{31{1'b0}}, comparator_1_gt};  // Bit_Extender bit_extender_1
  assign bit_extender_2_out = {{31{1'b0}}, comparator_1_eq};  // Bit_Extender bit_extender_2
  assign bit_extender_3_out = {{31{1'b0}}, comparator_1_lt};  // Bit_Extender bit_extender_3
  Multiplexer #(.select(4), .width(32)) multiplexer_3 (
    .in0(adder_1_out), .in1(subtractor_1_out), .in2(multiplier_1_out), .in3(divider_1_out), .in4(and_1_out),
    .in5(xor_1_out), .in6(or_1_out), .in7(bit_extender_1_out), .in8(bit_extender_2_out),
    .in9(bit_extender_3_out), .in10(shifter_1_out), .in11(shifter_2_out), .in12(shifter_3_out), .out(out_7),
    .sel(SELECTOR));  // open: in13, in14, in15, en
endmodule

// Decode Stage (D)
module Decode (
  input  [31:0] Instruction,
  output [6:0] OPCODE,
  output [4:0] RD,
  output [2:0] FUNCT3,
  output [4:0] RS1,
  output [4:0] RS2,
  output [6:0] FUNCT7,
  output [31:0] immediate
);

  wire comparator_1_eq, comparator_2_eq, comparator_3_eq;
  wire [1:0] adder_1_out, multiplexer_3_out, multiplexer_4_out, multiplexer_5_out, \type ;

  Comparator #(.width(7)) comparator_1 (.a(7'b0000011), .b(Instruction[6:0]), .eq(comparator_1_eq));  // open: gt, lt
  Comparator #(.width(7)) comparator_2 (.a(7'b0110011), .b(Instruction[6:0]), .eq(comparator_2_eq));  // open: gt, lt
  Comparator #(.width(7)) comparator_3 (.a(7'b0110111), .b(Instruction[6:0]), .eq(comparator_3_eq));  // open: gt, lt
  Multiplexer #(.select(2), .width(5)) multiplexer_1 (
    .in1(Instruction[11:7]), .in2(Instruction[11:7]), .out(RD), .sel(\type ));  // open: in0, in3, en
  Multiplexer #(.select(2), .width(3)) multiplexer_2 (
    .in1(Instruction[14:12]), .in2(Instruction[14:12]), .out(FUNCT3), .sel(\type ));  // open: in0, in3, en
  Multiplexer #(.width(2)) multiplexer_3 (
    .in0(2'b00), .in1(2'b10), .out(multiplexer_3_out), .sel(comparator_1_eq));  // open: en
  Multiplexer #(.width(2)) multiplexer_4 (
    .in0(2'b00), .in1(2'b01), .out(multiplexer_4_out), .sel(comparator_2_eq));  // open: en
  Multiplexer #(.width(2)) multiplexer_5 (
    .in0(2'b00), .in1(2'b11), .out(multiplexer_5_out), .sel(comparator_3_eq));  // open: en
  Multiplexer #(.select(2), .width(5)) multiplexer_6 (
    .in1(Instruction[19:15]), .in2(Instruction[19:15]), .out(RS1), .sel(\type ));  // open: in0, in3, en
  Adder #(.width(2)) adder_1 (.a(multiplexer_3_out), .b(multiplexer_4_out), .out(adder_1_out));  // open: cin, cout
  Multiplexer #(.select(2), .width(5)) multiplexer_7 (
    .in1(Instruction[24:20]), .in2({5{1'b0}}), .out(RS2), .sel(\type ));  // open: in0, in3, en
  Multiplexer #(.select(2), .width(7)) multiplexer_8 (
    .in1(Instruction[31:25]), .in2(Instruction[31:25]), .out(FUNCT7), .sel(\type ));  // open: in0, in3, en
  Adder #(.width(2)) adder_2 (.a(adder_1_out), .b(multiplexer_5_out), .out(\type ));  // open: cin, cout
  assign immediate = {{20{1'b0}}, Instruction[31:20]};  // Bit_Extender bit_extender_1

  assign OPCODE = Instruction[6:0];

  // Other names for the same wires on the sheet: immediate_t[11:0] = Instruction[31:20]; rs2Imm[31:0] = immediate
endmodule

module IF (
  input  [6:0] in_1,
  output [3:0] out_2
);

  Bit_Extender #(.in_width(7), .out_width(4)) bit_extender_1 (.in(in_1), .out(out_2));
  // Probe on nothing

  // Other names for the same wires on the sheet: Funct7_ID[6:0] = in_1
endmodule

module Register_File (
  input  [31:0] Write_Data,
  input  [4:0] RS1,
  input  [4:0] RS2,
  input  [4:0] RD,
  input  WrEn,
  input  clk,
  output [31:0] RS1_2,
  output [31:0] RS2_2,
  output [31:0] RD_2
);

  wire R0_En, R1_En, R2_En, R3_En, R4_En, R5_En, R6_En, R7_En;
  wire [31:0] R0, R1, R2, R3, R4, R5, R6, R7;

  Demultiplexer #(.select(5)) demultiplexer_1 (
    .out0(R0_En), .out1(R1_En), .out2(R2_En), .out3(R3_En), .out4(R4_En), .out5(R5_En), .out6(R6_En),
    .out7(R7_En), .in(WrEn), .sel(RD));  // open: out8, out9, out10, out11, out12, out13, out14, out15, out16, out17, out18, out19, out20, out21, out22, out23, out24, out25, out26, out27, out28, out29, out30, out31, en
  Register #(.width(32)) u_R0 (.D({32{1'b0}}), .en(R0_En), .Q(R0), .clk(clk));  // open: clr
  Register #(.width(32)) u_R1 (.D(Write_Data), .en(R1_En), .Q(R1), .clk(clk));  // open: clr
  Register #(.width(32)) u_R2 (.D(Write_Data), .en(R2_En), .Q(R2), .clk(clk));  // open: clr
  Register #(.width(32)) u_R3 (.D(Write_Data), .en(R3_En), .Q(R3), .clk(clk));  // open: clr
  Register #(.width(32)) u_R4 (.D(Write_Data), .en(R4_En), .Q(R4), .clk(clk));  // open: clr
  Register #(.width(32)) u_R5 (.D(Write_Data), .en(R5_En), .Q(R5), .clk(clk));  // open: clr
  Register #(.width(32)) u_R6 (.D(Write_Data), .en(R6_En), .Q(R6), .clk(clk));  // open: clr
  Register #(.width(32)) u_R7 (.D(Write_Data), .en(R7_En), .Q(R7), .clk(clk));  // open: clr
  Multiplexer #(.select(5), .width(32)) multiplexer_1 (
    .in0(R0), .in1(R1), .in2(R2), .in3(R3), .in4(R4), .in5(R5), .in6(R6), .in7(R7), .out(RS1_2), .sel(RS1));  // open: in8, in9, in10, in11, in12, in13, in14, in15, in16, in17, in18, in19, in20, in21, in22, in23, in24, in25, in26, in27, in28, in29, in30, in31, en
  Multiplexer #(.select(5), .width(32)) multiplexer_2 (
    .in0(R0), .in1(R1), .in2(R2), .in3(R3), .in4(R4), .in5(R5), .in6(R6), .in7(R7), .out(RS2_2), .sel(RS2));  // open: in8, in9, in10, in11, in12, in13, in14, in15, in16, in17, in18, in19, in20, in21, in22, in23, in24, in25, in26, in27, in28, in29, in30, in31, en
  Multiplexer #(.select(5), .width(32)) multiplexer_3 (
    .in0(R0), .in1(R1), .in2(R2), .in3(R3), .in4(R4), .in5(R5), .in6(R6), .in7(R7), .out(RD_2), .sel(RD));  // open: in8, in9, in10, in11, in12, in13, in14, in15, in16, in17, in18, in19, in20, in21, in22, in23, in24, in25, in26, in27, in28, in29, in30, in31, en
endmodule

module Control (
  input  [31:0] Instruction,
  input  BRLT,
  input  BREQ,
  output A_Sel,
  output B_Sel,
  output MemRW,
  output RWEn,
  output WrEn,
  output PC_Sel
);

  wire and_1_out, branch, comparator_1_eq, comparator_2_eq, comparator_3_eq, comparator_5_eq,
       comparator_6_eq, comparator_7_eq, comparator_8_eq, comparator_9_eq, comparator_10_eq,
       comparator_11_eq, comparator_12_eq;

  or or_1 (branch, BRLT, BREQ);
  Comparator #(.width(7)) comparator_1 (.a(Instruction[6:0]), .b(7'b0110011), .eq(comparator_1_eq));  // open: gt, lt
  Comparator #(.width(7)) comparator_2 (.a(Instruction[6:0]), .b(7'b0000011), .eq(comparator_2_eq));  // open: gt, lt
  Comparator #(.width(7)) comparator_3 (.a(Instruction[6:0]), .b(7'b0010011), .eq(comparator_3_eq));  // open: gt, lt
  Comparator #(.width(7)) comparator_4 (.a(Instruction[6:0]), .b(7'b0100011), .eq(MemRW));  // open: gt, lt
  Comparator #(.width(7)) comparator_5 (.a(Instruction[6:0]), .b(7'b0110111), .eq(comparator_5_eq));  // open: gt, lt
  Comparator #(.width(7)) comparator_6 (.a(Instruction[6:0]), .b(7'b1100011), .eq(comparator_6_eq));  // open: gt, lt
  Comparator #(.width(7)) comparator_7 (.a(Instruction[6:0]), .b(7'b1101111), .eq(comparator_7_eq));  // open: gt, lt
  Comparator #(.width(7)) comparator_8 (.a(Instruction[6:0]), .b(7'b1100111), .eq(comparator_8_eq));  // open: gt, lt
  and and_1 (and_1_out, branch, comparator_6_eq);
  or or_2 (A_Sel, comparator_1_eq, comparator_2_eq, comparator_3_eq, MemRW, comparator_8_eq);
  or or_3 (B_Sel, comparator_1_eq, comparator_3_eq, comparator_5_eq, comparator_6_eq, comparator_7_eq, comparator_8_eq);
  or or_4 (RWEn, MemRW, comparator_6_eq);
  or or_5 (PC_Sel, and_1_out, comparator_7_eq, comparator_8_eq);
  Comparator #(.width(7)) comparator_9 (.a(Instruction[6:0]), .b(7'b0110011), .eq(comparator_9_eq));  // open: gt, lt
  Comparator #(.width(7)) comparator_10 (.a(Instruction[6:0]), .b(7'b0000011), .eq(comparator_10_eq));  // open: gt, lt
  Comparator #(.width(7)) comparator_11 (.a(Instruction[6:0]), .b(7'b0110111), .eq(comparator_11_eq));  // open: gt, lt
  Comparator #(.width(7)) comparator_12 (.a(Instruction[6:0]), .b(7'b1101111), .eq(comparator_12_eq));  // open: gt, lt
  or or_6 (WrEn, comparator_9_eq, comparator_10_eq, comparator_11_eq, comparator_12_eq);

  // Other names for the same wires on the sheet: Opcode[6:0] = Instruction[6:0]; Funct3[2:0] = Instruction[14:12]
endmodule

module MEM (
  input  [4:0] Address,
  input  [31:0] Write_Data,
  input  WriteEn,
  input  clk,
  output [31:0] Read_Data
);

  wire and_1_out;

  buf and_1 (and_1_out, clk);  // AND_Gate
  RAM #(.addrWidth(5), .dataWidth(32), .bus("separate")) ram_1 (
    .addr(Address), .din(Write_Data), .data(Read_Data), .str(WriteEn), .sel(1'b1), .clk(and_1_out), .ld(1'b1));  // open: clr
endmodule

// Bypass_Logic
module bypassLogic (
  input  [4:0] rs12_D,
  input  [4:0] rd_EX,
  output out_3
);

  Comparator #(.width(5)) comparator_1 (.a(rs12_D), .b(rd_EX), .eq(out_3));  // open: gt, lt
endmodule
